// Logisim project projetoic.circ as structural Verilog: 3 circuits, main circuit somadorCompleto
module somadorCompleto (
  input  A,
  input  B,
  input  C,
  output Soma,
  output Carry_Out
);

  wire and_1_out, and_2_out, and_3_out, and_4_out, not_1_out, not_2_out, not_3_out, xor_1_out;

  not not_1 (not_1_out, A);
  not not_2 (not_2_out, B);
  not not_3 (not_3_out, C);
  xor xor_1 (xor_1_out, A, B);
  and and_1 (and_1_out, not_1_out, B, C);
  and and_2 (and_2_out, A, not_2_out, C);
  and and_3 (and_3_out, A, B, not_3_out);
  and and_4 (and_4_out, A, B, C);
  xor xor_2 (Soma, xor_1_out, C);
  or or_1 (Carry_Out, and_1_out, and_2_out, and_3_out, and_4_out);

  // Notes on the sheet:
  //   Somador Completo
endmodule

module main (
  input  A,
  input  A_2,
  input  B,
  input  B_2,
  input  C,
  input  Controle
);

  wire somadorcompleto_1_carry_out, somadorcompleto_1_soma, somadorcompleto_2_carry_out,
       somadorcompleto_2_soma;

  somadorCompleto somadorcompleto_1 (
    .A(A), .B(B), .C(C), .Soma(somadorcompleto_1_soma), .Carry_Out(somadorcompleto_1_carry_out));
  somadorCompleto somadorcompleto_2 (
    .A(A_2), .B(B_2), .C(somadorcompleto_1_carry_out), .Soma(somadorcompleto_2_soma),
    .Carry_Out(somadorcompleto_2_carry_out));
  multiplex multiplex_1 (.C(Controle));  // open: E0, E1, Saida
endmodule

module multiplex (
  input  E0,
  input  E1,
  input  C,
  output Saida
);

  wire and_1_out, and_2_out, not_1_out;

  not not_1 (not_1_out, C);
  and and_1 (and_1_out, E0, not_1_out);
  and and_2 (and_2_out, E1, C);
  or or_1 (Saida, and_1_out, and_2_out);
endmodule
